// Logisim project bcd_counter.circ as structural Verilog: 1 circuit, main circuit main
module main (
  input  in_1,
  output out_2,
  output out_3,
  output out_4,
  output out_5
);

  wire clock_1_out, nand_1_out;

  Clock clock_1 (.out(clock_1_out));
  T_Flip_Flop #(.trigger("falling")) t_ff_1 (
    .T(in_1), .clk(clock_1_out), .Q(out_5), .reset(nand_1_out), .preset(in_1));  // open: Qn
  T_Flip_Flop #(.trigger("falling")) t_ff_2 (
    .T(in_1), .clk(out_5), .Q(out_4), .reset(nand_1_out), .preset(in_1));  // open: Qn
  T_Flip_Flop #(.trigger("falling")) t_ff_3 (
    .T(in_1), .clk(out_4), .Q(out_3), .reset(nand_1_out), .preset(in_1));  // open: Qn
  T_Flip_Flop #(.trigger("falling")) t_ff_4 (
    .T(in_1), .clk(out_3), .Q(out_2), .reset(nand_1_out), .preset(in_1));  // open: Qn
  nand nand_1 (nand_1_out, out_4, out_2);
endmodule
