// Logisim project comparator_ka_project.circ as structural Verilog: 1 circuit, main circuit main
module main (
  input  A1,
  input  A0,
  input  B1,
  input  B0,
  output S,
  output E,
  output G
);

  wire and_1_out, and_2_out, and_3_out, and_4_out, and_5_out, and_6_out, not_1_out, not_2_out, not_3_out,
       not_4_out, xnor_1_out, xnor_2_out;

  not not_1 (not_1_out, A1);
  not not_2 (not_2_out, A0);
  not not_3 (not_3_out, B1);
  not not_4 (not_4_out, B0);
  and and_1 (and_1_out, not_1_out, not_2_out, B0);
  and and_2 (and_2_out, not_1_out, B1);
  and and_3 (and_3_out, not_2_out, B1, B0);
  xnor xnor_1 (xnor_1_out, A1, B1);
  xnor xnor_2 (xnor_2_out, A0, B0);
  and and_4 (and_4_out, A0, not_3_out, B0);
  and and_5 (and_5_out, A1, A0, not_4_out);
  and and_6 (and_6_out, A1, not_3_out);
  or or_1 (S, and_1_out, and_2_out, and_3_out);
  and and_7 (E, xnor_1_out, xnor_2_out);
  or or_2 (G, and_4_out, and_5_out, and_6_out);
endmodule
