// Logisim project dissss.circ as structural Verilog: 1 circuit, main circuit main
module main (
  input  D,
  input  C,
  input  B,
  input  A
);

  wire and_1_out, and_2_out, and_3_out, and_4_out, and_5_out, and_6_out, and_7_out, and_8_out, and_9_out,
       and_10_out, and_11_out, not_1_out, not_2_out, not_3_out, not_4_out, or_1_out, or_2_out, or_3_out,
       or_4_out, or_5_out, or_6_out, or_7_out, or_8_out, xnor_1_out, xor_1_out;

  not not_1 (not_1_out, D);
  not not_2 (not_2_out, C);
  not not_3 (not_3_out, B);
  not not_4 (not_4_out, A);
  xnor xnor_1 (xnor_1_out, A, C);
  and and_1 (and_1_out, A, B);
  and and_2 (and_2_out, not_4_out, not_3_out);
  and and_3 (and_3_out, not_4_out, B);
  and and_4 (and_4_out, not_2_out, B);
  and and_5 (and_5_out, not_4_out, not_2_out);
  or or_1 (or_1_out, B, not_2_out);
  or or_2 (or_2_out, not_4_out, not_3_out);
  and and_6 (and_6_out, not_4_out, not_3_out);
  and and_7 (and_7_out, or_1_out, not_4_out);
  and and_8 (and_8_out, or_2_out, C);
  xor xor_1 (xor_1_out, B, C);
  or or_3 (or_3_out, xnor_1_out, B, D);
  and and_9 (and_9_out, not_1_out, xor_1_out);
  and and_10 (and_10_out, B, not_4_out, not_1_out);
  and and_11 (and_11_out, A, not_3_out, C);
  or or_4 (or_4_out, and_1_out, and_2_out, not_2_out, D);
  or or_5 (or_5_out, A, not_3_out, C, D);
  or or_6 (or_6_out, and_8_out, and_6_out, D);
  or or_7 (or_7_out, and_9_out, and_10_out, D);
  or or_8 (or_8_out, and_3_out, and_4_out, and_11_out, and_5_out, D);
  _7_Segment_Display S (
    .g(or_7_out), .f(or_6_out), .a(or_3_out), .b(or_4_out), .e(and_7_out), .d(or_8_out), .c(or_5_out));  // open: dp
endmodule
