// Logisim project logic_gate_trainer.circ as structural Verilog: 1 circuit, main circuit main
module main (
  input  in_1,
  input  in_2,
  input  in_3,
  input  in_4,
  input  in_5,
  input  in_6,
  output out_7
);

  wire and_1_out, or_1_out, xnor_1_out, xor_1_out;

  and and_1 (and_1_out, in_4, in_3, in_2, in_1);
  or or_1 (or_1_out, in_4, in_3, in_2, in_1);
  ExactlyOne xor_1 (.out(xor_1_out), .in0(in_4), .in1(in_3), .in2(in_2), .in3(in_1));
  NotExactlyOne xnor_1 (.out(xnor_1_out), .in0(in_4), .in1(in_3), .in2(in_2), .in3(in_1));
  Multiplexer #(.select(2)) multiplexer_1 (
    .in0(and_1_out), .in1(or_1_out), .in2(xor_1_out), .in3(xnor_1_out), .out(out_7), .sel({in_5, in_6}));
endmodule
