// Logisim project traffic_light.circ as structural Verilog: 1 circuit, main circuit main
module main (
  input  in_1,
  input  in_2
);

  wire clock_1_out, decoder_1_out0, decoder_1_out1, decoder_1_out2, not_1_out, not_2_out, t_ff_1_q, t_ff_2_q;
  wire [1:0] and_1_out;

  Clock clock_1 (.out(clock_1_out));
  T_Flip_Flop t_ff_1 (.T(in_1), .clk(clock_1_out), .Q(t_ff_1_q));  // open: Qn, reset, preset
  not not_1 (not_1_out, t_ff_1_q);
  T_Flip_Flop t_ff_2 (.T(in_1), .clk(t_ff_1_q), .Q(t_ff_2_q));  // open: Qn, reset, preset
  not not_2 (not_2_out, t_ff_2_q);
  and and_1 (and_1_out[0], not_1_out, t_ff_2_q);
  and and_2 (and_1_out[1], t_ff_1_q, not_2_out);
  Decoder #(.select(2)) decoder_1 (
    .out0(decoder_1_out0), .out1(decoder_1_out1), .out2(decoder_1_out2), .sel(and_1_out), .en(in_2));  // open: out3
  LED led_1 (.in(decoder_1_out0));
  LED led_2 (.in(decoder_1_out1));
  LED led_3 (.in(decoder_1_out2));
endmodule
